# Fritzing sketch wiring-sketch (saved by Fritzing 0.9.5d)

parts:
  Grove1 = Grove OLED 128x96
  Part1 = Fingerprint Sensor
  A2 = DORHEA ESP32 GPIO breakout board 30pin
  U1 = ESP32-38PinWide [part_number=ESP32-38PinWide]  # not connected

nets:
  GND: Grove1.GND, Part1.GND, A2.Pin_27, A2.Pin_58, A2.Pin_85
  N1: Grove1.VCC, A2.Pin_86
  N2: Grove1.SDA, A2.Pin_87, A2.Pin_123
  N3: Grove1.SCL, A2.Pin_88, A2.Pin_126
  N4: Part1.VCC, A2.Pin_61
  N5: Part1.TX, A2.Pin_118
  N6: Part1.RX, A2.Pin_119

notes:
  FINGERPRINT SENSOR
  RED - VCC (3.3V) !!
  GREEN - GND
  BLACK - D16
  YELLOW - D17
  OLED DISPLAY
  GND - GND
  VCC - VCC
  SDA - D21
  SCL - D22

custom parts:
  Fingerprint Sensor: FINGERPRIN Sensor
  DORHEA ESP32 GPIO breakout board 30pin: ESP32 shield 30P expansion board, supports two power supply : DC 6.5-16v and USB 5.V
  ESP32-38PinWide: Generic 38-Pin ESP32 with wide format (only access to one side of pins on a breadboard) based on Stephen Lilley's HiLetgo ESP-WROOM-32 ESP32 ESP-32S Development Board.
